# Fritzing sketch typical (saved by Fritzing 0.9.3b)
breadboards: 1

parts:
  Part1 = Arduino Mega 2560 (Rev3)
  IR1 = TSOP312.., 314.. [package=THT]
  DS1 = DS18B20 1-Wire Temperature Sensor [part_number=DS18B20]
  Baro = Barometric Pressure Sensor - BMP180 Breakout (GY-68)
  DHT22 = Humidity and Temperature Sensor RHT03
  nRF = NRF24L01+ Breakout Board
  R1 = Resistor [tolerance=±5% resistance=4.7k package=THT]
  U1 = ESP8266 WiFi Module [part_number=ESP8266]

nets:
  N1: Part1.D20/SDA, Part1.SDA, Baro.SDA
  N2: Part1.SCL, Baro.SCL
  GND: Part1.GND, IR1.GND, DS1.GND, Baro.GND, DHT22.GND_2, nRF.GND, U1.GND
  N3: Part1.D10_PWM, nRF.CS
  N4: Part1.D9_PWM, nRF.CE
  VCC: Part1.3V3, nRF.VCC, U1.VCC
  VCC_2: Part1.5V, IR1.Vs, DS1.VDD, Baro.VCC, DHT22.Vcc, R1.Pin_1
  N5: Part1.D2_PWM, DHT22.Data-signal
  N6: Part1.D3_PWM, IR1.Data
  N7: Part1.D4_PWM, DS1.DQ, R1.Pin_0
  N8: Part1.D50, nRF.MISO
  N9: Part1.D51, nRF.MOSI
  N10: Part1.D52, nRF.SCK
